# Fritzing sketch Untitled Sketch 7 (saved by Fritzing 0.9.4)

parts:
  Part1 = Adafruit Trinket M0 [part_number="Adafruit #3500"]
  J1 = Basic Servo

nets:
  GND: Part1.GND, J1.gnd
  N1: Part1.D1_A0_PA02, J1.pulse
  N2: Part1.VBUS, J1.vcc
